// Logisim project bit4subandsom.circ as structural Verilog: 16 circuits, main circuit somador de 1bit
module ula_completa2 (
  input  [3:0] a,
  input  [3:0] b,
  input  d,
  input  [2:0] operacao,
  output overflow,
  output zero,
  output [3:0] out_7
);

  // Probe on a
  ula_completa ula_completa_1 (
    .d(d), .A(a), .B(b), .operacao(operacao), .out_6(out_7), .zero(zero), .overflow(overflow));
  // Probe on b
  // Probe on out_7
endmodule

module ula_completa (
  input  d,
  input  [3:0] A,
  input  [3:0] B,
  input  [2:0] operacao,
  output overflow,
  output [3:0] out_6,
  output zero
);

  wire and_1_out, and_2_out, decod_3x8_1_s0, decod_3x8_1_s1, decod_3x8_1_s2, decod_3x8_1_s3, decod_3x8_1_s4,
       decod_3x8_1_s5, decod_3x8_1_s6, decod_3x8_1_s7, not_1_out, somador_4_bits_1_out_4, sub_4bits_1_out_4;
  wire [3:0] buffer3stage_1_out_3, buffer3stage_5_out_3, or_4bits_1_out_3, rotacao_a_direita_1_out_3,
       rotacao_a_esquerda_1_a_b_c_d_2, somador_4_bits_1_out_5, sub_4bits_1_out_5;

  or or_1 (overflow, and_1_out, and_2_out);
  and and_1 (and_1_out, somador_4_bits_1_out_4, decod_3x8_1_s1);
  and and_2 (and_2_out, sub_4bits_1_out_4, decod_3x8_1_s2);
  decod_3x8 decod_3x8_1 (
    .operation(operacao), .s0(decod_3x8_1_s0), .s1(decod_3x8_1_s1), .s2(decod_3x8_1_s2), .s3(decod_3x8_1_s3),
    .s4(decod_3x8_1_s4), .s5(decod_3x8_1_s5), .s6(decod_3x8_1_s6), .S7(decod_3x8_1_s7));
  buffer3stage buffer3stage_1 (.in_1(B), .in_2(decod_3x8_1_s0), .out_3(buffer3stage_1_out_3));
  nor nor_1 (zero, decod_3x8_1_s7, decod_3x8_1_s6, buffer3stage_1_out_3[0], buffer3stage_1_out_3[1], buffer3stage_1_out_3[2], buffer3stage_1_out_3[3]);
  somador_4_bits somador_4_bits_1 (
    .in_2(A), .in_3(1'b0), .out_4(somador_4_bits_1_out_4), .in_1(B), .out_5(somador_4_bits_1_out_5));
  buffer3stage buffer3stage_2 (.in_1(somador_4_bits_1_out_5), .in_2(decod_3x8_1_s1), .out_3(buffer3stage_1_out_3));
  sub_4bits sub_4bits_1 (.in_2(A), .in_3(1'b0), .out_4(sub_4bits_1_out_4), .in_1(B), .out_5(sub_4bits_1_out_5));
  buffer3stage buffer3stage_3 (.in_1(sub_4bits_1_out_5), .in_2(decod_3x8_1_s2), .out_3(buffer3stage_1_out_3));
  OR_4BITS or_4bits_1 (.in_1(A), .in_2(B), .out_3(or_4bits_1_out_3));
  buffer3stage buffer3stage_4 (.in_1(or_4bits_1_out_3), .in_2(decod_3x8_1_s3), .out_3(buffer3stage_1_out_3));
  buffer_3_stage_inversor buffer_3_stage_inversor_1 (.in_1(B), .in_2(decod_3x8_1_s4), .out_3(out_6));
  not not_1 (not_1_out, d);
  buffer3stage buffer3stage_5 (.in_1(rotacao_a_direita_1_out_3), .in_2(d), .out_3(buffer3stage_5_out_3));
  rotacao_a_direita rotacao_a_direita_1 (.in_1(A), .in_2(B[1:0]), .out_3(rotacao_a_direita_1_out_3));
  buffer3stage buffer3stage_6 (.in_1(rotacao_a_esquerda_1_a_b_c_d_2), .in_2(not_1_out), .out_3(buffer3stage_5_out_3));
  rotacao_a_esquerda rotacao_a_esquerda_1 (.a_b_c_d(A), .x_y(B[1:0]), .a_b_c_d_2(rotacao_a_esquerda_1_a_b_c_d_2));
  buffer3stage buffer3stage_7 (.in_1(buffer3stage_5_out_3), .in_2(decod_3x8_1_s5), .out_3(buffer3stage_1_out_3));
endmodule

module ula (
  input  [3:0] a,
  input  [3:0] b,
  input  d,
  input  [2:0] operacao,
  output out_5,
  output out_6,
  output [3:0] s
);

  circuito_parcial_ula circuito_parcial_ula_1 (
    .d(d), .A(a), .B(b), .out_5(out_5), .out_6(out_6), .in_4(operacao), .s(s));
endmodule

module circuito_parcial_ula (
  input  d,
  input  [3:0] A,
  input  [3:0] B,
  input  [2:0] in_4,
  output out_5,
  output out_6,
  output [3:0] s
);

  wire decod_3x8_1_s0, decod_3x8_1_s1, decod_3x8_1_s2, decod_3x8_1_s3, decod_3x8_1_s4, decod_3x8_1_s5,
       not_1_out;
  wire [3:0] buffer3stage_5_out_3, or_4bits_1_out_3, rotacao_a_direita_1_out_3,
       rotacao_a_esquerda_1_a_b_c_d_2, somador_4_bits_1_out_5, sub_4bits_1_out_5;

  decod_3x8 decod_3x8_1 (
    .operation(in_4), .s0(decod_3x8_1_s0), .s1(decod_3x8_1_s1), .s2(decod_3x8_1_s2), .s3(decod_3x8_1_s3),
    .s4(decod_3x8_1_s4), .s5(decod_3x8_1_s5));  // open: s6, S7
  buffer3stage buffer3stage_1 (.in_1(B), .in_2(decod_3x8_1_s0), .out_3(s));
  somador_4_bits somador_4_bits_1 (.in_2(A), .in_3(1'b0), .out_4(out_6), .in_1(B), .out_5(somador_4_bits_1_out_5));
  buffer3stage buffer3stage_2 (.in_1(somador_4_bits_1_out_5), .in_2(decod_3x8_1_s1), .out_3(s));
  sub_4bits sub_4bits_1 (.in_2(A), .in_3(1'b0), .out_4(out_5), .in_1(B), .out_5(sub_4bits_1_out_5));
  buffer3stage buffer3stage_3 (.in_1(sub_4bits_1_out_5), .in_2(decod_3x8_1_s2), .out_3(s));
  OR_4BITS or_4bits_1 (.in_1(B), .in_2(B), .out_3(or_4bits_1_out_3));
  buffer3stage buffer3stage_4 (.in_1(or_4bits_1_out_3), .in_2(decod_3x8_1_s3), .out_3(s));
  buffer_3_stage_inversor buffer_3_stage_inversor_1 (.in_1(B), .in_2(decod_3x8_1_s4), .out_3(s));
  not not_1 (not_1_out, d);
  buffer3stage buffer3stage_5 (.in_1(rotacao_a_direita_1_out_3), .in_2(d), .out_3(buffer3stage_5_out_3));
  rotacao_a_direita rotacao_a_direita_1 (.in_1(A), .in_2(B[1:0]), .out_3(rotacao_a_direita_1_out_3));
  rotacao_a_esquerda rotacao_a_esquerda_1 (.a_b_c_d(A), .x_y(B[1:0]), .a_b_c_d_2(rotacao_a_esquerda_1_a_b_c_d_2));
  buffer3stage buffer3stage_6 (.in_1(rotacao_a_esquerda_1_a_b_c_d_2), .in_2(not_1_out), .out_3(buffer3stage_5_out_3));
  buffer3stage buffer3stage_7 (.in_1(buffer3stage_5_out_3), .in_2(decod_3x8_1_s5), .out_3(s));
endmodule

module OR_4BITS (
  input  [3:0] in_1,
  input  [3:0] in_2,
  output [3:0] out_3
);

  or or_1 (out_3[3], in_1[0], in_2[3]);
  or or_2 (out_3[2], in_1[1], in_2[2]);
  or or_3 (out_3[1], in_1[2], in_2[1]);
  or or_4 (out_3[0], in_1[3], in_2[0]);
endmodule

module circuito_parcial_da_ula (
  input  [3:0] A,
  input  [3:0] B,
  input  [2:0] operacoes,
  output [3:0] s
);

  wire decod_3x8_1_s0, decod_3x8_1_s1, decod_3x8_1_s2, decod_3x8_1_s4, decod_3x8_1_s5;
  wire [3:0] rotacao_a_esquerda_1_a_b_c_d_2, somador_4_bits_1_out_5, sub_4bits_1_out_5;

  decod_3x8 decod_3x8_1 (
    .operation(operacoes), .s0(decod_3x8_1_s0), .s1(decod_3x8_1_s1), .s2(decod_3x8_1_s2),
    .s4(decod_3x8_1_s4), .s5(decod_3x8_1_s5));  // open: s3, s6, S7
  buffer3stage buffer3stage_1 (.in_1(B), .in_2(decod_3x8_1_s0), .out_3(s));
  somador_4_bits somador_4_bits_1 (.in_2(A), .in_3(1'b0), .in_1(B), .out_5(somador_4_bits_1_out_5));  // open: out_4
  buffer3stage buffer3stage_2 (.in_1(somador_4_bits_1_out_5), .in_2(decod_3x8_1_s1), .out_3(s));
  sub_4bits sub_4bits_1 (.in_2(A), .in_3(1'b0), .in_1(B), .out_5(sub_4bits_1_out_5));  // open: out_4
  buffer3stage buffer3stage_3 (.in_1(sub_4bits_1_out_5), .in_2(decod_3x8_1_s2), .out_3(s));
  buffer_3_stage_inversor buffer_3_stage_inversor_1 (.in_1(B), .in_2(decod_3x8_1_s4), .out_3(s));
  rotacao_a_esquerda rotacao_a_esquerda_1 (.a_b_c_d(A), .x_y(B[1:0]), .a_b_c_d_2(rotacao_a_esquerda_1_a_b_c_d_2));
  buffer_3_stage_inversor buffer_3_stage_inversor_2 (
    .in_1(rotacao_a_esquerda_1_a_b_c_d_2), .in_2(decod_3x8_1_s5), .out_3(s));
endmodule

module cicuito_parcial_ula (
  input  [3:0] A,
  input  [3:0] B,
  input  [2:0] in_3,
  output out_4,
  output out_5,
  output [3:0] s
);

  wire decod_3x8_1_s0, decod_3x8_1_s1, decod_3x8_1_s2, decod_3x8_1_s4;
  wire [3:0] somador_4_bits_1_out_5, sub_4bits_1_out_5;

  decod_3x8 decod_3x8_1 (
    .operation(in_3), .s0(decod_3x8_1_s0), .s1(decod_3x8_1_s1), .s2(decod_3x8_1_s2), .s4(decod_3x8_1_s4));  // open: s3, s5, s6, S7
  buffer3stage buffer3stage_1 (.in_1(B), .in_2(decod_3x8_1_s0), .out_3(s));
  somador_4_bits somador_4_bits_1 (.in_2(A), .in_3(1'b0), .out_4(out_5), .in_1(B), .out_5(somador_4_bits_1_out_5));
  buffer3stage buffer3stage_2 (.in_1(somador_4_bits_1_out_5), .in_2(decod_3x8_1_s1), .out_3(s));
  sub_4bits sub_4bits_1 (.in_2(A), .in_3(1'b0), .out_4(out_4), .in_1(B), .out_5(sub_4bits_1_out_5));
  buffer3stage buffer3stage_3 (.in_1(sub_4bits_1_out_5), .in_2(decod_3x8_1_s2), .out_3(s));
  buffer_3_stage_inversor buffer_3_stage_inversor_1 (.in_1(B), .in_2(decod_3x8_1_s4), .out_3(s));

  // Notes on the sheet:
  //   out_5: pull=up
endmodule

module rotacao_a_direita (
  input  [3:0] in_1,
  input  [1:0] in_2,
  output [3:0] out_3
);

  wire and_1_out, and_2_out, and_3_out, and_4_out, and_5_out, and_6_out, and_7_out, and_8_out, and_9_out;

  and and_1 (and_1_out, ~in_2[1], ~in_2[0], in_1[0]);  // AND_Gate
  and and_2 (and_2_out, ~in_2[1], in_2[0], in_1[1]);  // AND_Gate
  and and_3 (and_3_out, in_2[1], ~in_2[0], in_1[2]);  // AND_Gate
  and and_4 (and_4_out, in_2[1], in_2[0], in_1[3]);
  buf and_5 (and_5_out, in_1[1]);  // AND_Gate AND_Gate
  and and_6 (and_6_out, ~in_2[1], in_2[0], in_1[2]);  // AND_Gate
  and and_7 (and_7_out, in_2[1], ~in_2[0], in_1[3]);  // AND_Gate
  and and_8 (and_8_out, ~in_2[1], ~in_2[0], in_1[2]);  // AND_Gate
  and and_9 (and_9_out, in_2[1], ~in_2[0], in_1[3]);  // AND_Gate
  and and_10 (out_3[3], ~in_2[1], ~in_2[0], in_1[3]);  // AND_Gate
  or or_1 (out_3[0], and_1_out, and_2_out, and_3_out, and_4_out);
  or or_2 (out_3[1], and_5_out, and_6_out, and_7_out);
  or or_3 (out_3[2], and_8_out, and_9_out);
endmodule

module rotacao_a_esquerda (
  input  [3:0] a_b_c_d,
  input  [1:0] x_y,
  output [3:0] a_b_c_d_2
);

  wire and_1_out, and_2_out, and_3_out, and_4_out, and_5_out, and_6_out, and_7_out, and_8_out, and_9_out;

  and and_1 (and_1_out, ~x_y[1], ~x_y[0], a_b_c_d[3]);  // AND_Gate
  and and_2 (and_2_out, ~x_y[1], x_y[0], a_b_c_d[2]);  // AND_Gate
  and and_3 (and_3_out, x_y[1], ~x_y[0], a_b_c_d[1]);  // AND_Gate
  and and_4 (and_4_out, x_y[1], x_y[0], a_b_c_d[0]);
  buf and_5 (and_5_out, a_b_c_d[2]);  // AND_Gate AND_Gate
  and and_6 (and_6_out, ~x_y[1], x_y[0], a_b_c_d[1]);  // AND_Gate
  and and_7 (and_7_out, x_y[1], ~x_y[0], a_b_c_d[0]);  // AND_Gate
  and and_8 (and_8_out, ~x_y[1], ~x_y[0], a_b_c_d[1]);  // AND_Gate
  and and_9 (and_9_out, x_y[1], ~x_y[0], a_b_c_d[0]);  // AND_Gate
  and and_10 (a_b_c_d_2[0], ~x_y[1], ~x_y[0], a_b_c_d[0]);  // AND_Gate
  or or_1 (a_b_c_d_2[3], and_1_out, and_2_out, and_3_out, and_4_out);
  or or_2 (a_b_c_d_2[2], and_5_out, and_6_out, and_7_out);
  or or_3 (a_b_c_d_2[1], and_8_out, and_9_out);
endmodule

module decod_3x8 (
  input  [2:0] operation,
  output s0,
  output s1,
  output s2,
  output s3,
  output s4,
  output s5,
  output s6,
  output S7
);

  wire not_1_out, not_2_out, not_3_out, not_4_out, not_5_out, not_6_out, not_7_out, not_8_out, not_9_out,
       not_10_out, not_11_out, not_12_out;

  not not_1 (not_1_out, operation[0]);
  not not_2 (not_2_out, operation[1]);
  not not_3 (not_3_out, operation[2]);
  not not_4 (not_4_out, operation[0]);
  not not_5 (not_5_out, operation[2]);
  not not_6 (not_6_out, operation[1]);
  not not_7 (not_7_out, operation[2]);
  not not_8 (not_8_out, operation[1]);
  not not_9 (not_9_out, operation[0]);
  not not_10 (not_10_out, operation[2]);
  not not_11 (not_11_out, operation[0]);
  not not_12 (not_12_out, operation[1]);
  and and_1 (S7, operation[0], operation[1], operation[2]);
  and and_2 (s0, not_1_out, not_2_out, not_3_out);
  and and_3 (s1, not_4_out, not_8_out, operation[2]);
  and and_4 (s2, not_9_out, operation[1], not_10_out);
  and and_5 (s3, not_11_out, operation[1], operation[2]);
  and and_6 (s4, operation[0], not_12_out, not_5_out);
  and and_7 (s5, operation[0], not_6_out, operation[2]);
  and and_8 (s6, operation[0], operation[1], not_7_out);
endmodule

module buffer_3_stage_inversor (
  input  [3:0] in_1,
  input  in_2,
  output [3:0] out_3
);

  assign out_3[2] = in_2 ? ~in_1[2] : 1'bz;  // Controlled_Inverter controlled_inverter_1
  assign out_3[3] = in_2 ? ~in_1[3] : 1'bz;  // Controlled_Inverter controlled_inverter_2
  assign out_3[1] = in_2 ? ~in_1[1] : 1'bz;  // Controlled_Inverter controlled_inverter_3
  assign out_3[0] = in_2 ? ~in_1[0] : 1'bz;  // Controlled_Inverter controlled_inverter_4
endmodule

module buffer3stage (
  input  [3:0] in_1,
  input  in_2,
  output [3:0] out_3
);

  assign out_3[2] = in_2 ? in_1[2] : 1'bz;  // Controlled_Buffer controlled_buffer_1
  assign out_3[3] = in_2 ? in_1[3] : 1'bz;  // Controlled_Buffer controlled_buffer_2
  assign out_3[0] = in_2 ? in_1[0] : 1'bz;  // Controlled_Buffer controlled_buffer_3
  assign out_3[1] = in_2 ? in_1[1] : 1'bz;  // Controlled_Buffer controlled_buffer_4
endmodule

module sub_4bits (
  input  [3:0] in_1,
  input  [3:0] in_2,
  input  in_3,
  output out_4,
  output [3:0] out_5
);

  wire subtrator_1_s, subtrator_2_s, subtrator_3_s;

  subtrator subtrator_1 (.a(in_2[3]), .b(in_1[3]), .in_3(in_3), .s(subtrator_1_s), .vai1(out_5[3]));
  subtrator subtrator_2 (.a(in_2[2]), .b(in_1[2]), .in_3(subtrator_1_s), .s(subtrator_2_s), .vai1(out_5[2]));
  subtrator subtrator_3 (.a(in_2[1]), .b(in_1[1]), .in_3(subtrator_2_s), .s(subtrator_3_s), .vai1(out_5[1]));
  subtrator subtrator_4 (.a(in_2[0]), .b(in_1[0]), .in_3(subtrator_3_s), .s(out_4), .vai1(out_5[0]));
endmodule

module subtrator (
  input  a,
  input  b,
  input  in_3,
  output s,
  output vai1
);

  wire and_1_out, and_2_out, not_1_out, or_1_out, xor_1_out;

  not not_1 (not_1_out, in_3);
  xor xor_1 (xor_1_out, a, b);
  or or_1 (or_1_out, b, in_3);
  and and_1 (and_1_out, b, in_3);
  and and_2 (and_2_out, or_1_out, not_1_out);
  xor xor_2 (s, xor_1_out, in_3);
  or or_2 (vai1, and_2_out, and_1_out);
endmodule

module somador_4_bits (
  input  [3:0] in_1,
  input  [3:0] in_2,
  input  in_3,
  output out_4,
  output [3:0] out_5
);

  wire somador_de_1bit_1_s, somador_de_1bit_2_s, somador_de_1bit_3_s;

  somador_de_1bit somador_de_1bit_1 (.a(in_1[3]), .b(in_2[3]), .vem1(in_3), .s(somador_de_1bit_1_s), .vai1(out_5[3]));
  somador_de_1bit somador_de_1bit_2 (
    .a(in_1[2]), .b(in_2[2]), .vem1(somador_de_1bit_1_s), .s(somador_de_1bit_2_s), .vai1(out_5[2]));
  somador_de_1bit somador_de_1bit_3 (
    .a(in_1[1]), .b(in_2[1]), .vem1(somador_de_1bit_2_s), .s(somador_de_1bit_3_s), .vai1(out_5[1]));
  somador_de_1bit somador_de_1bit_4 (.a(in_1[0]), .b(in_2[0]), .vem1(somador_de_1bit_3_s), .s(out_4), .vai1(out_5[0]));
endmodule

module somador_de_1bit (
  input  a,
  input  b,
  input  vem1,
  output s,
  output vai1
);

  wire and_1_out, and_2_out, or_1_out, xor_1_out;

  xor xor_1 (xor_1_out, a, b);
  or or_1 (or_1_out, b, vem1);
  and and_1 (and_1_out, b, vem1);
  and and_2 (and_2_out, or_1_out, a);
  xor xor_2 (s, xor_1_out, vem1);
  or or_2 (vai1, and_2_out, and_1_out);
endmodule
